# Fritzing sketch 6586 (saved by Fritzing 1.0.2b)
breadboards: 1

parts:
  M1 = DC Motor [voltage_(max)=6V voltage_(min)=3V]  # not connected
  R1 = Resistor [tolerance=±5% power=0.25W resistance=220 package=THT]
  S1 = Pushbutton [package="[THT]"]
  GND-3V-D0-D1-D2-D3-VT = Camdenboss CTB0158-7 [part_number=- package=THT]  # not connected
  A1_-A2 = Camdenboss CTB0158-2 [part_number=. package=THT]  # not connected
  B1_-_B2 = Camdenboss CTB0158-2 [part_number=. package=THT]  # not connected
  IN+_IN- = Camdenboss CTB0158-2 [part_number=. package=THT]  # not connected

nets:
  N1: R1.Pin_0, S1.Pin_1, S1.Pin_2

notes:
  MOTEUR1 MOTEUR2
