# Fritzing sketch L298N (saved by Fritzing 1.0.2b)
breadboards: 1

parts:
  S1 = H-Bridge with L298N
  S3 = Pushbutton [package="[THT]"]
  R2 = Resistor [tolerance=±5% resistance=10k package="2010 [SMD]"]
  VCC1 = 4 x AAA Battery Mount
  R3 = Resistor [tolerance=±5% power=0.25W resistance=10k package=THT]  # not connected
  S4 = Pushbutton [package="[THT]"]
  M1 = DC Motor [voltage_(max)=6V voltage_(min)=3V]

nets:
  12V: S1.12V, S1.5V, S3.Pin_1, S3.Pin_2, VCC1.+, S4.Pin_1, S4.Pin_2
  N1: S1.GND, R2.Pin_0, VCC1.-
  N2: S1.IN1, S3.Pin_3, S3.Pin_4
  N3: S1.IN2, R2.Pin_1, S4.Pin_3, S4.Pin_4
  N4: S1.OUT3-Motor2, M1.pin_2
  N5: S1.OUT4-Motor2, M1.pin_1

custom parts:
  H-Bridge with L298N: h-bridge
