# Fritzing sketch LCD_PARALELLE_SCHEMA (saved by Fritzing 1.0.2b)
breadboards: 1

parts:
  LCD1 = LCD screen
  R1 = Rotary Potentiometer (Large) [maximum_resistance=10kΩ knob_status=50% power=0.5W package=THT]
  R2 = Resistor [tolerance=±5% power=0.25W resistance=220 package=THT]
  Composant1 = Arduino Uno (Rev3)

nets:
  VSS: LCD1.VSS, LCD1.R/W, LCD1.LED-, R1.leg2, Composant1.GND
  VDD: LCD1.VDD, R1.leg1, R2.Pin_0, Composant1.5V
  N1: LCD1.V0, R1.wiper
  N2: LCD1.RS, Composant1.D12/MISO
  N3: LCD1.E, Composant1.D11_PWM/MOSI
  N4: LCD1.DB4, Composant1.D5_PWM
  N5: LCD1.DB5, Composant1.D4
  N6: LCD1.DB6, Composant1.D3_PWM
  N7: LCD1.DB7, Composant1.D2
  N8: LCD1.LED+, R2.Pin_1
